# Fritzing sketch Flashing Circuit (saved by Fritzing 1.0.0rc)
circuit board: 3.03698cm x 5cm
breadboards: 1

parts:
  C1 = Electrolytic Capacitor [capacitance=1µF voltage=50V package="100 mil [THT, electrolytic]"]
  U1 = 555 Timer [mn=NE555 mpn=C695838 package="DIP8 [THT]"]
  C2 = Ceramic Capacitor [capacitance=100nF rated_voltage=35V voltage=35V mpn=C2896072 package="200 mil [THT, multilayer]"]
  R2_1 = Resistor [tolerance=±5% power=0.5W resistance=47k mpn=C274539 package=THT]
  R3 = Resistor [tolerance=±5% power=0.25 resistance=2.2k mpn=C70772 package=THT]
  R2 = Resistor [tolerance=±5% power=0.25 resistance=680k mpn=C714343 package=THT]
  R1 = Resistor [tolerance=±5% resistance=2.2k power=0.25 mpn=C70772 package=THT]
  Q1 = Basic FET N-Channel [mn=IRLZ44N mpn=C38774 package="TO220 [THT]"]
  Vout_GND = Spring Terminal 2.54 2 [package=THT]
  Vtrig = Spring Terminal 2.54 1 [package=THT]
  C3 = Ceramic Capacitor [capacitance=100nF rated_voltage=35V voltage=35V mpn=C2896072 package="200 mil [THT, multilayer]"]
  GND_Vin = Spring Terminal 2.54 2 [package=THT]
  U2 = TRIMPOT [maximum_resistance=1MΩ knob_status=50% power=0.25W package=trimpot_pth_s3_lock]

nets:
  GND: C1.-, U1.Ground, C2.0, Vout_GND.pin3, Vout_GND.pin4, C3.0, GND_Vin.pin1, GND_Vin.pin2
  N1: C1.+, U1.Trigger, U1.Threshold, R2.Pin_0, U2.CW
  N2: U1.Output, R3.Pin_0
  N3: U1.Reset, U1.Vcc_Supply_Voltage, R1.Pin_1, Q1.source
  N4: U1.Control_Voltage, C2.1
  N5: U1.Discharge, R2_1.Pin_0, R1.Pin_0, U2.WIPER
  N6: R2_1.Pin_1, R2.Pin_1
  Vout: R3.Pin_1, Vout_GND.pin1, Vout_GND.pin2
  Vtrig: Q1.gate, Vtrig.pin1, Vtrig.pin2
  Vin: Q1.drain, C3.1, GND_Vin.pin3, GND_Vin.pin4

notes:
  Ouput: 200mA MAX
  Vcc: 4.5-18V MAX
  INPUT/OUTPUT: 5-15V
  TRIG: GND=Start, Vdd=Stop
  TRIG: High=Start, Low=Stop
  R2: LED Brightness (mA)
  V1.0
  Pat Fleming
  R1/R2/C1: Flash Rate
  Flasher Circuit, Flasher Circuit for Layout Lights, Warning flashers, Emergency / Police Vechicles, etc, 1.0
  Flasher Circuit
  Flash Circuit - Specs:
  - 0.5 sec flashing rate (R2 ~ 680k ohm
  - Connections:
  1) Vin/GND - layout accessory bus
  2) TRIG - Arduino/Switch (start/stop flasher)
  3) Vout/GND - LED(s)
  Trigger (Vtrig):
  High (V+) = Start
  Low (GND) = Stop
  Flash Rate:
  - Change R2 value(s) or Trimpot:
  - See 555 Timer Calculator: https://www.digikey.com/en/resources/conversion-calculators/conversion-calculator-555-timer

// code stored in the sketch: Flasher_Circuit.ino
const int buttonPin = 2; // Button connected to digital pin 2
const int ledPin = 13;   // LED connected to digital pin 13

void setup() {
  pinMode(buttonPin, INPUT_PULLUP); // Set the button pin as input with internal pull-up resistor
  pinMode(ledPin, OUTPUT);          // Set the LED pin as output
}

void loop() {
  // Check if the button is pressed (active LOW)
  if (digitalRead(buttonPin) == LOW) {
    digitalWrite(ledPin, HIGH); // Turn on the Flasher Circuit
  } else {
    digitalWrite(ledPin, LOW);  // Turn off the Flasher Circuit
  }
}
